// Logisim project counter.circ as structural Verilog: 1 circuit, main circuit main
module main (
  output [15:0] out_1
);

  wire clock_1_out;
  wire [15:0] adder_1_out, undriven, undriven_2;

  Clock clock_1 (.out(clock_1_out));
  Adder #(.width(16)) adder_1 (.a(undriven), .b(undriven_2), .out(adder_1_out));  // open: cin, cout
  Register #(.width(16)) register_1 (.D(adder_1_out), .Q(out_1));  // open: en, clk, clr

  // Notes on the sheet:
  //   clock
  //   adder
  //   register
endmodule
